# Fritzing sketch SparkBot_PCB_Main-4.0 (saved by Fritzing 0.9.2b)
circuit board: 4.4cm x 10cm

parts:
  J1 = female pin header, 12 pins [form="♀ (female)"]
  J2 = female pin header, 12 pins [form="♀ (female)"]
  P1 = Piezo Speaker
  RGB = RGB LED (com. cathode, rbg) [package="5 mm [THT]"]
  B2 = female pin header, 2 pins [form="♀ (female)"]
  B1 = female pin header, 2 pins [form="♀ (female)"]
  R1 = Resistor [tolerance=±5% resistance=220 package=THT]
  I/O = female pin header, 9 pins [form="♀ (female)"]
  LDR = Photocell (LDR) [package=THT]
  MIC = Breakout Board for Electret Microphone
  RST = female pin header, 2 pins [form="♀ (female)"]
  Nano = Arduino Nano (Rev3.0)
  J3 = double row female pin header, 30 pins [form="♀ (female)"]
  RI1 = Basic Servo
  LE1 = Basic Servo
  H1 = Basic Servo
  R = female pin header, 4 pins [form="♀ (female)"]
  B = female pin header, 4 pins [form="♀ (female)"]
  G = female pin header, 4 pins [form="♀ (female)"]
  J4 = double row female pin header, 30 pins [form="♀ (female)"]

nets:
  N1: J1.pin2, R1.Pin_1, MIC.GND
  N2: J1.pin3, Nano.D0/RX, J4.pin2, J4.pin29
  N3: J1.pin4, Nano.D1/TX, J4.pin1, J4.pin30
  N4: J1.pin5, RGB.green_anode
  N5: J1.pin6, I/O.pin7
  N6: J1.pin7, I/O.pin8
  N7: J1.pin8, I/O.pin9
  N8: J1.pin9, MIC.VCC
  N9: J1.pin10, I/O.pin5
  N10: J1.pin11, I/O.pin6
  N11: J1.pin12, J2.pin5, J2.pin6, B2.pin1, B1.pin1, R1.Pin_0, LDR.pin_0
  N12: J2.pin1, B2.pin2, B1.pin2, I/O.pin2, LDR.pin_1, MIC.AUD
  N13: J2.pin2, RST.pin1
  N14: J2.pin4, P1.pin1, RGB.common_cathode, I/O.pin1, RST.pin2
  N15: J2.pin7, I/O.pin4
  N16: J2.pin8, I/O.pin3
  N17: J2.pin9, RGB.red_anode
  N18: J2.pin10, RGB.blue_anode
  N19: J2.pin12, P1.pin2
  N20: Nano.RESET, J3.pin3, J3.pin28, J4.pin3, J4.pin28
  GND: Nano.GND, J3.pin2, J3.pin29, RI1.gnd, LE1.gnd, H1.gnd, R.pin3, B.pin3, G.pin3, J4.pin4, J4.pin27
  N21: Nano.D2, J4.pin5, J4.pin26
  N22: Nano.D3, R.pin1, B.pin1, G.pin1, J4.pin6, J4.pin25
  N23: Nano.D4, J4.pin7, J4.pin24
  N24: Nano.D5, R.pin2, B.pin2, G.pin2, J4.pin8, J4.pin23
  N25: Nano.D6, R.pin4, B.pin4, G.pin4, J4.pin9, J4.pin22
  N26: Nano.D7, J4.pin10, J4.pin21
  N27: Nano.D8, J4.pin11, J4.pin20
  N28: Nano.D9, H1.pulse, J4.pin12, J4.pin19
  N29: Nano.D10, LE1.pulse, J4.pin13, J4.pin18
  N30: Nano.D11/MOSI, RI1.pulse, J4.pin14, J4.pin17
  N31: Nano.D12/MISO, J4.pin15, J4.pin16
  N32: Nano.VIN, J3.pin1, J3.pin30
  VCC: Nano.5V, J3.pin4, J3.pin27, RI1.vcc, LE1.vcc, H1.vcc
  N33: Nano.A7, J3.pin5, J3.pin26
  N34: Nano.A6, J3.pin6, J3.pin25
  N35: Nano.A5, J3.pin7, J3.pin24
  N36: Nano.A4, J3.pin8, J3.pin23
  N37: Nano.A3, J3.pin9, J3.pin22
  N38: Nano.A2, J3.pin10, J3.pin21
  N39: Nano.A1, J3.pin11, J3.pin20
  N40: Nano.A0, J3.pin12, J3.pin19
  N41: Nano.AREF, J3.pin13, J3.pin18
  N42: Nano.3V3, J3.pin14, J3.pin17
  N43: Nano.D13/SCK, J3.pin15, J3.pin16

notes:
  GND
  4
  3
  2
  1
  0
  3v3
  G
  SparkBot
  GPIO
  The IoT robotics kit for everyone.
  R
  L
  Photon
  |
  /\
  servos
  5
  6
  v4.0
  tx
  rx
  VIN
  5V
  3V3
  ANALOG
  A0
  7
  RST
