# Fritzing sketch SparkBot_PCB_Main (saved by Fritzing 0.9.2b)
circuit board: 4cm x 4cm

parts:
  J1 = female pin header, 12 pins [form="♀ (female)"]
  J2 = female pin header, 12 pins [form="♀ (female)"]
  Buzzer = Piezo Speaker
  Microphone = female pin header, 3 pins [form="♀ (female)"]
  I/O = female pin header, 5 pins [form="♀ (female)"]
  Arm_Servo_1 = Basic Servo
  Arm_Servo_2 = Basic Servo
  Head_Servo = Basic Servo
  RGB_Moodlights = RGB LED (com. cathode, rbg) [package="5 mm [THT]"]
  Button_2 = female pin header, 2 pins [form="♀ (female)"]
  Button_1 = female pin header, 2 pins [form="♀ (female)"]
  Temperature_Sensor = female pin header, 3 pins [form="♀ (female)"]
  R1 = Resistor [tolerance=±5% resistance=220 package="2512 [SMD]"]
  Battery = Battery block 9V

nets:
  N1: J1.pin1, Battery.+
  GND: J1.pin2, Buzzer.pin1, Microphone.pin1, I/O.pin1, Arm_Servo_1.gnd, Arm_Servo_2.gnd, Head_Servo.gnd, RGB_Moodlights.common_cathode, Temperature_Sensor.pin1, Battery.-
  N2: J1.pin7, J2.pin5, Button_2.pin1, Button_1.pin1, R1.Pin_1
  N3: J1.pin8, I/O.pin4
  N4: J1.pin9, I/O.pin3
  N5: J1.pin10, I/O.pin2
  N6: J1.pin11, Microphone.pin2
  N7: J1.pin12, Buzzer.pin2
  VCC: J2.pin1, Microphone.pin3, I/O.pin5, Arm_Servo_1.vcc, Arm_Servo_2.vcc, Head_Servo.vcc, Temperature_Sensor.pin3, R1.Pin_0
  N8: J2.pin4, Button_2.pin2, Button_1.pin2
  N9: J2.pin6, RGB_Moodlights.green_anode
  N10: J2.pin7, RGB_Moodlights.blue_anode
  N11: J2.pin8, RGB_Moodlights.red_anode
  N12: J2.pin9, Temperature_Sensor.pin2
  N13: J2.pin10, Head_Servo.pulse
  N14: J2.pin11, Arm_Servo_2.pulse
  N15: J2.pin12, Arm_Servo_1.pulse
