# Fritzing sketch SparkBot-main (saved by Fritzing 0.9.1b)
perfboards: 8

parts:
  LED1 = RGB LED (com. cathode, rbg) [package="5 mm [THT]"]  # not connected
  LED2 = RGB LED (com. cathode, rbg) [package="5 mm [THT]"]  # not connected
  LED4 = RGB LED (com. cathode, rbg) [package="5 mm [THT]"]  # not connected
  J1 = female pin header, 4 pins [form="♀ (female)"]
  J2 = female pin header, 4 pins [form="♀ (female)"]
  J3 = female pin header, 4 pins [form="♀ (female)"]
  LED3 = RGB LED (com. cathode, rbg) [package="5 mm [THT]"]  # not connected
  J5 = female pin header, 12 pins [form="♀ (female)"]
  J4 = female pin header, 12 pins [form="♀ (female)"]
  Part1 = Spark Core (v1.0)
  J6 = female pin header, 4 pins [form="♀ (female)"]
  J7 = female pin header, 4 pins [form="♀ (female)"]  # not connected
  J8 = female pin header, 4 pins [form="♀ (female)"]
  J9 = female pin header, 4 pins [form="♀ (female)"]
  J10 = Basic Servo  # not connected
  J11 = Basic Servo  # not connected
  J12 = Basic Servo  # not connected
  J13 = Piezo Speaker  # not connected
  S1 = Momentary Switch [package=ksa_sealed_tac_switch]  # not connected
  S2 = Momentary Switch [package=ksa_sealed_tac_switch]  # not connected
  R1 = Resistor [package="2512 [SMD]"]  # not connected
  R2 = Resistor [package="2512 [SMD]"]  # not connected
  U1 = TEMPERATURE-SENSOR [package=to-92]  # not connected
  Part2 = Breakout Board for Electret Microphone  # not connected
  J14 = female pin header, 5 pins [form="♀ (female)"]  # not connected

nets:
  N1: J1.pin1, J9.pin4
  N2: J1.pin2, J9.pin3
  N3: J1.pin3, J9.pin2
  N4: J1.pin4, J9.pin1
  N5: J2.pin1, J6.pin4
  N6: J2.pin2, J6.pin3
  N7: J2.pin3, J6.pin2
  N8: J2.pin4, J6.pin1
  N9: J3.pin1, J8.pin4
  N10: J3.pin2, J8.pin3
  N11: J3.pin3, J8.pin2
  N12: J3.pin4, J8.pin1
  N13: J5.pin1, Part1.D0
  N14: J5.pin2, Part1.D1
  N15: J5.pin3, Part1.D2
  N16: J5.pin4, Part1.D3
  N17: J5.pin5, Part1.D4
  N18: J5.pin6, Part1.D5
  N19: J5.pin7, Part1.D6
  N20: J5.pin8, Part1.D7
  N21: J5.pin9, J4.pin11, Part1.GND
  N22: J5.pin10, Part1.3V3*
  N23: J5.pin11, Part1.RST
  N24: J5.pin12, Part1.3V3
  N25: J4.pin1, Part1.A0
  N26: J4.pin2, Part1.A1
  N27: J4.pin3, Part1.A2
  N28: J4.pin4, Part1.A3
  N29: J4.pin5, Part1.A4
  N30: J4.pin6, Part1.A5
  N31: J4.pin7, Part1.A6
  N32: J4.pin8, Part1.A7
  N33: J4.pin9, Part1.TX
  N34: J4.pin10, Part1.RX
  N35: J4.pin12, Part1.VIN
